// Logisim project ALU.circ as structural Verilog: 1 circuit, main circuit ALU
module ALU (
  input  [31:0] in_1,
  input  [31:0] in_2,
  input  [31:0] in_3,
  input  [3:0] Operation
);

  wire Equals, Greater_Than, Less_Than;
  wire [31:0] Add, AND, Div, Mult, NAND, NOR, OR, Sub, XNOR, XOR;

  Adder #(.width(32)) adder_1 (.a(in_1), .b(in_3), .out(Add));  // open: cin, cout
  Multiplier #(.width(32)) multiplier_1 (.a(in_1), .b(in_3), .out(Mult));  // open: cin, cout
  Comparator #(.width(32)) comparator_1 (.a(in_1), .b(in_3), .gt(Greater_Than), .eq(Equals), .lt(Less_Than));
  Subtractor #(.width(32)) subtractor_1 (.a(in_1), .b(in_3), .out(Sub));  // open: bin, bout
  Divider #(.width(32)) divider_1 (.a(in_1), .b(in_3), .out(Div));  // open: upper, rem
  assign AND = in_1 & in_3;  // AND_Gate and_1, 32 bits wide
  assign OR = in_1 | in_3;  // OR_Gate or_1, 32 bits wide
  assign XOR = in_1 ^ in_3;  // XOR_Gate xor_1, 32 bits wide
  Multiplexer #(.select(4), .width(32)) multiplexer_1 (
    .in0(Add), .in1(Sub), .in2(Mult), .in3(Div), .in4(AND), .in5(NOR), .in6(XOR), .in7(OR), .in8(NAND),
    .in9(XNOR), .out(in_2), .sel(Operation));  // open: in10, in11, in12, in13, in14, in15, en
  assign NAND = ~(in_1 & in_3);  // NAND_Gate nand_1, 32 bits wide
  assign NOR = ~(in_1 | in_3);  // NOR_Gate nor_1, 32 bits wide
  assign XNOR = ~(in_1 ^ in_3);  // XNOR_Gate xnor_1, 32 bits wide

  // Other names for the same wires on the sheet: A[31:0] = in_1; ALU_Output[31:0] = in_2; B[31:0] = in_3;
  //   Selector[3:0] = Operation

  // Notes on the sheet:
  //   Inputs
  //   Data
  //   Arithmetic
  //   Outputs
  //   Logic
endmodule
