// Logisim project Control Unit.circ as structural Verilog
module ALU_Control (
  input  [5:0] Input,
  input  [5:0] in_2,
  output [3:0] out_3
);

  wire _00_0000, Add, add_t, addi, And, and_t, andi, comparator_1_eq, comparator_2_eq, comparator_3_eq,
       comparator_4_eq, comparator_5_eq, comparator_6_eq, comparator_12_eq, comparator_13_eq,
       comparator_14_eq, comparator_15_eq, comparator_16_eq, comparator_17_eq, div, divu, mult, mulu, \nor ,
       Or, or_t, ori, priority_encoder_1_gs, Slt, slt_t, slti, sltiu, Sltu, sltu_t, sub, Xor, xor_t, xori;
  wire [3:0] priority_encoder_1_out;

  Comparator #(.width(6)) comparator_1 (.a(in_2), .b(6'b100000), .eq(comparator_1_eq));  // open: gt, lt
  Comparator #(.width(6)) comparator_2 (.a(in_2), .b(6'b011010), .eq(comparator_2_eq));  // open: gt, lt
  Comparator #(.width(6)) comparator_3 (.a(in_2), .b(6'b100111), .eq(comparator_3_eq));  // open: gt, lt
  Comparator #(.width(6)) comparator_4 (.a(in_2), .b(6'b100010), .eq(comparator_4_eq));  // open: gt, lt
  Comparator #(.width(6)) comparator_5 (.a(in_2), .b(6'b011011), .eq(comparator_5_eq));  // open: gt, lt
  Comparator #(.width(6)) comparator_6 (.a(in_2), .b(6'b101000), .eq(comparator_6_eq));  // open: gt, lt
  Comparator #(.width(6)) comparator_7 (.a(Input), .b(6'b001000), .eq(addi));  // open: gt, lt
  Comparator #(.width(6)) comparator_8 (.a(Input), .b(6'b001010), .eq(slti));  // open: gt, lt
  and and_1 (add_t, _00_0000, comparator_1_eq);
  and and_2 (div, _00_0000, comparator_2_eq);
  and and_3 (\nor , _00_0000, comparator_3_eq);
  and and_4 (sub, _00_0000, comparator_4_eq);
  and and_5 (divu, _00_0000, comparator_5_eq);
  and and_6 (xor_t, _00_0000, comparator_6_eq);
  Comparator #(.width(6)) comparator_9 (.a(Input), .b(6'b001100), .eq(andi));  // open: gt, lt
  Comparator #(.width(6)) comparator_10 (.a(Input), .b(6'b001011), .eq(sltiu));  // open: gt, lt
  Comparator #(.width(6)) comparator_11 (.a(Input), .b({6{1'b0}}), .eq(_00_0000));  // open: gt, lt
  and and_7 (mult, _00_0000, comparator_12_eq);
  Comparator #(.width(6)) comparator_12 (.a(in_2), .b(6'b011000), .eq(comparator_12_eq));  // open: gt, lt
  and and_8 (and_t, _00_0000, comparator_13_eq);
  Comparator #(.width(6)) comparator_13 (.a(in_2), .b(6'b100100), .eq(comparator_13_eq));  // open: gt, lt
  and and_9 (slt_t, _00_0000, comparator_14_eq);
  Comparator #(.width(6)) comparator_14 (.a(in_2), .b(6'b101010), .eq(comparator_14_eq));  // open: gt, lt
  and and_10 (mulu, _00_0000, comparator_15_eq);
  Comparator #(.width(6)) comparator_15 (.a(in_2), .b(6'b011001), .eq(comparator_15_eq));  // open: gt, lt
  and and_11 (or_t, _00_0000, comparator_16_eq);
  Comparator #(.width(6)) comparator_16 (.a(in_2), .b(6'b100101), .eq(comparator_16_eq));  // open: gt, lt
  and and_12 (sltu_t, _00_0000, comparator_17_eq);
  Comparator #(.width(6)) comparator_17 (.a(in_2), .b(6'b101011), .eq(comparator_17_eq));  // open: gt, lt
  Comparator #(.width(6)) comparator_18 (.a(Input), .b(6'b001101), .eq(ori));  // open: gt, lt
  Comparator #(.width(6)) comparator_19 (.a(Input), .b(6'b001110), .eq(xori));  // open: gt, lt
  or or_1 (Add, add_t, addi);
  or or_2 (And, and_t, andi);
  or or_3 (Or, or_t, ori);
  Priority_Encoder #(.select(4)) priority_encoder_1 (
    .in0(Add), .in1(sub), .in2(Slt), .in3(Sltu), .in4(And), .in5(Or), .in6(\nor ), .in7(Xor), .in8(mult),
    .in9(mulu), .in10(div), .in11(divu), .out(priority_encoder_1_out), .gs(priority_encoder_1_gs),
    .en_in(1'b1));  // open: in12, in13, in14, in15, en_out
  or or_4 (Sltu, sltiu, sltu_t);
  or or_5 (Slt, slt_t, slti);
  or or_6 (Xor, xor_t, xori);
  Multiplexer #(.width(4), .enable("false")) multiplexer_1 (
    .in0(4'b0000), .in1(priority_encoder_1_out), .out(out_3), .sel(priority_encoder_1_gs));

  // Other names for the same wires on the sheet: ALU_Selector[3:0] = out_3; Func_Code[5:0] = in_2;
  //   Op_Code[5:0] = Input

  // Notes on the sheet:
  //   Type I
  //   Type R
  //   Output
endmodule

module Type_I (
  input  [5:0] Input,
  output out_2
);

  wire _00_0000, _00_0010, _11_1000, _11_1111;

  Comparator #(.width(6)) comparator_1 (.a(Input), .b({6{1'b0}}), .eq(_00_0000));  // open: gt, lt
  Comparator #(.width(6)) comparator_2 (.a(Input), .b({6{1'b1}}), .eq(_11_1111));  // open: gt, lt
  Comparator #(.width(6)) comparator_3 (.a(Input), .b(6'b111000), .eq(_11_1000));  // open: gt, lt
  Comparator #(.width(6)) comparator_4 (.a(Input), .b(6'b000010), .eq(_00_0010));  // open: gt, lt
  nor nor_1 (out_2, _00_0000, _11_1111, _11_1000, _00_0010);

  // Other names for the same wires on the sheet: Op_Code[5:0] = Input; Type_I = out_2

  // Notes on the sheet:
  //   Output
endmodule

module BC_Selector (
  input  [5:0] Input,
  input  [5:0] in_2,
  output [2:0] Jump_Condition,
  output [1:0] Branch_Selector
);

  wire _00_0000, beq, bgtz, blez, bltz, bne, comparator_4_eq, IsBranch, j, jr;
  wire [2:0] priority_encoder_1_out;

  Comparator #(.width(6)) comparator_1 (.a(Input), .b(6'b000100), .eq(beq));  // open: gt, lt
  Comparator #(.width(6)) comparator_2 (.a(Input), .b(6'b000110), .eq(blez));  // open: gt, lt
  Comparator #(.width(6)) comparator_3 (.a(Input), .b(6'b000001), .eq(bltz));  // open: gt, lt
  Comparator #(.width(6)) comparator_4 (.a(in_2), .b(6'b001000), .eq(comparator_4_eq));  // open: gt, lt
  Comparator #(.width(6)) comparator_5 (.a(Input), .b(6'b000101), .eq(bne));  // open: gt, lt
  Comparator #(.width(6)) comparator_6 (.a(Input), .b(6'b000111), .eq(bgtz));  // open: gt, lt
  Comparator #(.width(6)) comparator_7 (.a(Input), .b(6'b000010), .eq(j));  // open: gt, lt
  and and_1 (jr, _00_0000, comparator_4_eq);
  Comparator #(.width(6)) comparator_8 (.a(Input), .b({6{1'b0}}), .eq(_00_0000));  // open: gt, lt
  or or_1 (Branch_Selector[1], jr, j);
  Priority_Encoder priority_encoder_1 (
    .in0(beq), .in1(bne), .in2(bgtz), .in3(blez), .in4(bltz), .out(priority_encoder_1_out), .en_in(1'b1),
    .gs(IsBranch));  // open: in5, in6, in7, en_out
  or or_2 (Branch_Selector[0], IsBranch, jr);
  Multiplexer #(.width(3), .enable("false")) multiplexer_1 (
    .in0(3'b000), .in1(priority_encoder_1_out), .out(Jump_Condition), .sel(IsBranch));

  // Other names for the same wires on the sheet: Func_Code[5:0] = in_2; Op_Code[5:0] = Input
endmodule

module Program_Counter (
  input  in_1,
  input  in_2,
  input  in_3,
  input  [31:0] in_4,
  output [31:0] out_5
);

  Register #(.width(32)) register_1 (.D(in_4), .en(in_2), .Q(out_5), .clk(in_1), .clr(in_3));

  // Other names for the same wires on the sheet: Clock = in_1; Enable = in_2; Reset = in_3
endmodule

module Branch_Control (
  input  [31:0] in_1,
  input  [31:0] in_2,
  input  [31:0] in_3,
  input  [25:0] in_4,
  input  [1:0] in_5,
  input  [2:0] in_6,
  input  [15:0] in_7,
  output [31:0] PC_Input
);

  wire comparator_2_eq, multiplexer_1_out, tunnel, tunnel_t, tunnel_t_t, tunnel_t_t_t, tunnel_t_t_t_t;
  wire [13:0] bit_extender_1_out;
  wire [31:0] multiplexer_2_out, PC___4, PC___4___4_x_Offset;

  Adder #(.width(32)) adder_1 (.a(in_3), .b(32'h4), .out(PC___4));  // open: cin, cout
  assign bit_extender_1_out = {{13{in_7[15]}}, in_7[15]};  // Bit_Extender bit_extender_1
  Adder #(.width(32)) adder_2 (
    .a(PC___4), .b({bit_extender_1_out, in_7, 2'b00}), .out(PC___4___4_x_Offset));  // open: cin, cout
  Comparator #(.width(32)) comparator_1 (.a(in_1), .b(in_2), .eq(tunnel_t_t_t));  // open: gt, lt
  Comparator #(.width(32)) comparator_2 (
    .a(in_1), .b({32{1'b0}}), .gt(tunnel_t_t_t_t), .eq(comparator_2_eq), .lt(tunnel_t));
  not not_1 (tunnel, tunnel_t_t_t);
  or or_1 (tunnel_t_t, comparator_2_eq, tunnel_t);
  Multiplexer #(.select(3), .enable("false")) multiplexer_1 (
    .in0(tunnel_t_t_t), .in1(tunnel), .in2(tunnel_t_t_t_t), .in3(tunnel_t_t), .in4(tunnel_t),
    .out(multiplexer_1_out), .sel(in_6));  // open: in5, in6, in7
  Multiplexer #(.width(32), .enable("false")) multiplexer_2 (
    .in0(PC___4), .in1(PC___4___4_x_Offset), .out(multiplexer_2_out), .sel(multiplexer_1_out));
  Multiplexer #(.select(2), .width(32), .enable("false")) multiplexer_3 (
    .in0(PC___4), .in1(multiplexer_2_out), .in2({in_3[31:28], in_4, 2'b00}), .in3(in_1), .out(PC_Input),
    .sel(in_5));

  // Other names for the same wires on the sheet: Offset[15:0] = in_7; Branch_Selector[1:0] = in_5;
  //   Destiny[25:0] = in_4; Jump[31:2] = {in_3[31:28], in_4}; PC[31:0] = in_3; Jump_Condition[2:0] = in_6;
  //   RS[31:0] = in_1; RT[31:0] = in_2
endmodule
