// Logisim project Data Path.circ as structural Verilog: 5 circuits, main circuit Data Path
module Data_Path (
  input  [6:0] in_1,
  input  [31:0] in_2,
  input  [15:0] in_3,
  input  in_4,
  input  in_5,
  input  in_6,
  input  in_7,
  input  in_8,
  input  in_9,
  input  in_10,
  input  in_11,
  input  [4:0] in_12,
  input  [3:0] in_13,
  input  [4:0] in_14,
  input  in_15,
  input  [4:0] in_16,
  input  in_17,
  input  [2:0] in_18,
  input  in_19,
  output [31:0] out_20,
  output [31:0] out_21,
  output [31:0] out_22,
  output [31:0] out_23,
  output [31:0] out_24,
  output [6:0] out_25
);


  // Other names for the same wires on the sheet: A_Selector[4:0] = in_14; ALU_Out[31:0] = out_21;
  //   ALU_Selector[3:0] = in_13; B_Selector[4:0] = in_16; Clk = in_17; Const[15:0] = in_3; Const_Extend = in_15;
  //   Data_Address[4:0] = in_12; Hi_Lo_en = in_6; kbd_Data[6:0] = in_1; kbd_en = in_10; PC_en = in_7; pop = in_5;
  //   push = in_4; R_W_en = in_8; RAM_Data[31:0] = in_2; RAM_Write_Data[31:0] = out_20; Reset = in_19;
  //   RF_Selector[2:0] = in_18; RS[31:0] = out_22; RT[31:0] = out_24; SP[31:0] = out_23; sw = in_9;
  //   tty_Data[6:0] = out_25; Type_I = in_11

  // Notes on the sheet:
  //   Input
  //   Output
endmodule

module Branch_Control (
  input  [31:0] in_1,
  input  [31:0] in_2,
  input  [31:0] in_3,
  input  [25:0] in_4,
  input  [1:0] in_5,
  input  [2:0] in_6,
  input  [15:0] in_7,
  output [31:0] out_8
);

  wire comparator_2_eq, multiplexer_2_out, tunnel, tunnel_t, tunnel_t_t, tunnel_t_t_t, tunnel_t_t_t_t;
  wire [13:0] bit_extender_1_out;
  wire [31:0] multiplexer_1_out, PC___4, PC___4___4_x_Offset;

  Adder #(.width(32)) adder_1 (.a(in_3), .b(32'h4), .out(PC___4));  // open: cin, cout
  assign bit_extender_1_out = {{13{in_7[15]}}, in_7[15]};  // Bit_Extender bit_extender_1
  Adder #(.width(32)) adder_2 (
    .a(PC___4), .b({bit_extender_1_out, in_7, 2'b00}), .out(PC___4___4_x_Offset));  // open: cin, cout
  Comparator #(.width(32)) comparator_1 (.a(in_1), .b(in_2), .eq(tunnel_t_t_t));  // open: gt, lt
  Comparator #(.width(32)) comparator_2 (
    .a(in_1), .b({32{1'b0}}), .gt(tunnel_t_t_t_t), .eq(comparator_2_eq), .lt(tunnel_t));
  not not_1 (tunnel, tunnel_t_t_t);
  or or_1 (tunnel_t_t, comparator_2_eq, tunnel_t);
  Multiplexer #(.width(32), .enable("false")) multiplexer_1 (
    .in0(PC___4), .in1(PC___4___4_x_Offset), .out(multiplexer_1_out), .sel(multiplexer_2_out));
  Multiplexer #(.select(3), .enable("false")) multiplexer_2 (
    .in0(tunnel_t_t_t), .in1(tunnel), .in2(tunnel_t_t_t_t), .in3(tunnel_t_t), .in4(tunnel_t),
    .out(multiplexer_2_out), .sel(in_6));  // open: in5, in6, in7
  Multiplexer #(.select(2), .width(32), .enable("false")) multiplexer_3 (
    .in0(PC___4), .in1(multiplexer_1_out), .in2({in_3[31:28], in_4, 2'b00}), .in3(in_1), .out(out_8),
    .sel(in_5));

  // Other names for the same wires on the sheet: Offset[15:0] = in_7; Branch_Selector[1:0] = in_5;
  //   Destiny[25:0] = in_4; Jump[31:2] = {in_3[31:28], in_4}; PC[31:0] = in_3; Jump_Condition[2:0] = in_6;
  //   PC_Input[31:0] = out_8; RS[31:0] = in_1; RT[31:0] = in_2

  // Notes on the sheet:
  //   Input
  //   Output
endmodule

module Program_Counter (
  input  in_1,
  input  in_2,
  input  in_3,
  input  [31:0] in_4,
  output [31:0] out_5
);

  Register #(.width(32)) register_1 (.D(in_4), .en(in_2), .Q(out_5), .clk(in_1), .clr(in_3));

  // Other names for the same wires on the sheet: Clock = in_1; Enable = in_2; Reset = in_3
endmodule

module ALU_Input (
  input  [31:0] in_1,
  input  [15:0] in_2,
  input  in_3
);


  // Other names for the same wires on the sheet: Const[15:0] = in_2; Const_Extender_Selector = in_3; RT[31:0] = in_1

  // Notes on the sheet:
  //   Input
endmodule

module Const_Extender (
  input  in_1
);


  // Other names for the same wires on the sheet: Const_Extender_Selector = in_1
endmodule
