// Logisim project HILO.circ as structural Verilog: 1 circuit, main circuit HILO
module HILO (
  input  Hi_Lo_enable,
  input  Clock,
  input  [31:0] in_3,
  input  [31:0] in_4,
  output [31:0] Low_Output,
  output [31:0] HighOutput
);

  Register #(.width(32)) Low (.D(in_4), .en(Hi_Lo_enable), .Q(Low_Output), .clk(Clock));  // open: clr
  Register #(.width(32)) High (.D(in_3), .en(Hi_Lo_enable), .Q(HighOutput), .clk(Clock));  // open: clr

  // Other names for the same wires on the sheet: clk = Clock; en = Hi_Lo_enable; H_Input[31:0] = in_3;
  //   L_Input[31:0] = in_4

  // Notes on the sheet:
  //   High input
  //   Low input
  //   HI-LO
endmodule
