// Logisim project Register File.circ as structural Verilog: 1 circuit, main circuit Register file
module Register_file (
  input  [31:0] in_1,
  input  clock,
  input  PC_enable,
  input  reset,
  input  pop,
  input  push,
  input  r_w,
  input  [4:0] Data_Address,
  input  [4:0] Selector_A,
  input  [4:0] Selector_B
);

  wire L0, L1, L2, L3, L4, L5, L6, L7, L8, L9, L10, L11, L12, L13, L14, L15, L16, L17, L18, L19, L20, L21,
       L22, L23, L24, L25, L26, L27, L28, L29, L30;
  wire [31:0] A, B, Q0, Q1, Q2, Q3, Q4, Q5, Q6, Q7, Q8, Q9, Q10, Q11, Q12, Q13, Q14, Q15, Q16, Q17, Q18, Q19,
       Q20, Q21, Q22, Q23, Q24, Q25, Q26, Q27, Q28, Q29, Q30;

  Demultiplexer #(.select(5), .enable("false")) demultiplexer_1 (
    .out0(L0), .out1(L1), .out2(L2), .out3(L3), .out4(L4), .out5(L5), .out6(L6), .out7(L7), .out8(L8),
    .out9(L9), .out10(L10), .out11(L11), .out12(L12), .out13(L13), .out14(L14), .out15(L15), .out16(L16),
    .out17(L17), .out18(L18), .out19(L19), .out20(L20), .out21(L21), .out22(L22), .out23(L23), .out24(L24),
    .out25(L25), .out26(L26), .out27(L27), .out28(L28), .out29(L29), .out30(L30), .in(r_w), .sel(Data_Address));  // open: out31
  Multiplexer #(.select(5), .width(32), .enable("false")) multiplexer_1 (
    .in0(Q0), .in1(Q1), .in2(Q2), .in3(Q3), .in4(Q4), .in5(Q5), .in6(Q6), .in7(Q7), .in8(Q8), .in9(Q9),
    .in10(Q10), .in11(Q11), .in12(Q12), .in13(Q13), .in14(Q14), .in15(Q15), .in16(Q16), .in17(Q17),
    .in18(Q18), .in19(Q19), .in20(Q20), .in21(Q21), .in22(Q22), .in23(Q23), .in24(Q24), .in25(Q25),
    .in26(Q26), .in27(Q27), .in28(Q28), .in29(Q29), .in30(Q30), .out(A), .sel(Selector_A));  // open: in31
  Register #(.width(32)) R0 (.D(in_1), .en(L0), .Q(Q0), .clk(clock), .clr(reset));
  Register #(.width(32)) R8 (.D(in_1), .en(L8), .Q(Q8), .clk(clock), .clr(reset));
  Register #(.width(32)) R0_2 (.D(in_1), .en(L16), .Q(Q16), .clk(clock), .clr(reset));
  Register #(.width(32)) R0_3 (.D(in_1), .en(L24), .Q(Q24), .clk(clock), .clr(reset));
  Register #(.width(32)) R1 (.D(in_1), .en(L1), .Q(Q1), .clk(clock), .clr(reset));
  Register #(.width(32)) R9 (.D(in_1), .en(L9), .Q(Q9), .clk(clock), .clr(reset));
  Register #(.width(32)) R0_4 (.D(in_1), .en(L17), .Q(Q17), .clk(clock), .clr(reset));
  Register #(.width(32)) R0_5 (.D(in_1), .en(L25), .Q(Q25), .clk(clock), .clr(reset));
  Multiplexer #(.select(5), .width(32), .enable("false")) multiplexer_2 (
    .in0(Q0), .in1(Q1), .in2(Q2), .in3(Q3), .in4(Q4), .in5(Q5), .in6(Q6), .in7(Q7), .in8(Q8), .in9(Q9),
    .in10(Q10), .in11(Q11), .in12(Q12), .in13(Q13), .in14(Q14), .in15(Q15), .in16(Q16), .in17(Q17),
    .in18(Q18), .in19(Q19), .in20(Q20), .in21(Q21), .in22(Q22), .in23(Q23), .in24(Q24), .in25(Q25),
    .in26(Q26), .in27(Q27), .in28(Q28), .in29(Q29), .in30(Q30), .out(B), .sel(Selector_B));  // open: in31
  Register #(.width(32)) R2 (.D(in_1), .en(L2), .Q(Q2), .clk(clock), .clr(reset));
  Register #(.width(32)) R10 (.D(in_1), .en(L10), .Q(Q10), .clk(clock), .clr(reset));
  Register #(.width(32)) R0_6 (.D(in_1), .en(L18), .Q(Q18), .clk(clock), .clr(reset));
  Register #(.width(32)) R0_7 (.D(in_1), .en(L26), .Q(Q26), .clk(clock), .clr(reset));
  Register #(.width(32)) R3 (.D(in_1), .en(L3), .Q(Q3), .clk(clock), .clr(reset));
  Register #(.width(32)) R11 (.D(in_1), .en(L11), .Q(Q11), .clk(clock), .clr(reset));
  Register #(.width(32)) R0_8 (.D(in_1), .en(L19), .Q(Q19), .clk(clock), .clr(reset));
  Register #(.width(32)) R0_9 (.D(in_1), .en(L27), .Q(Q27), .clk(clock), .clr(reset));
  Register #(.width(32)) R4 (.D(in_1), .en(L4), .Q(Q4), .clk(clock), .clr(reset));
  Register #(.width(32)) R12 (.D(in_1), .en(L12), .Q(Q12), .clk(clock), .clr(reset));
  Register #(.width(32)) R0_10 (.D(in_1), .en(L20), .Q(Q20), .clk(clock), .clr(reset));
  Register #(.width(32)) R0_11 (.D(in_1), .en(L28), .Q(Q28), .clk(clock), .clr(reset));
  Register #(.width(32)) R5 (.D(in_1), .en(L5), .Q(Q5), .clk(clock), .clr(reset));
  Register #(.width(32)) R0_12 (.D(in_1), .en(L13), .Q(Q13), .clk(clock), .clr(reset));
  Register #(.width(32)) R0_13 (.D(in_1), .en(L21), .Q(Q21), .clk(clock), .clr(reset));
  Register #(.width(32)) R0_14 (.D(in_1), .en(L29), .Q(Q29), .clk(clock), .clr(reset));
  Register #(.width(32)) R6 (.D(in_1), .en(L6), .Q(Q6), .clk(clock), .clr(reset));
  Register #(.width(32)) R0_15 (.D(in_1), .en(L14), .Q(Q14), .clk(clock), .clr(reset));
  Register #(.width(32)) R0_16 (.D(in_1), .en(L22), .Q(Q22), .clk(clock), .clr(reset));
  Register #(.width(32)) R0_17 (.D(in_1), .en(L30), .Q(Q30), .clk(clock), .clr(reset));
  Register #(.width(32)) R7 (.D(in_1), .en(L7), .Q(Q7), .clk(clock), .clr(reset));
  Register #(.width(32)) R0_18 (.D(in_1), .en(L15), .Q(Q15), .clk(clock), .clr(reset));
  Register #(.width(32)) R0_19 (.D(in_1), .en(L23), .Q(Q23), .clk(clock), .clr(reset));

  // Other names for the same wires on the sheet: clk = clock; DA[4:0] = Data_Address; Data_Input[31:0] = in_1;
  //   PC_en = PC_enable; Select_A[4:0] = Selector_A; Select_B[4:0] = Selector_B

  // Notes on the sheet:
  //   Data Input
  //   Input
  //   Register File
  //   Output
endmodule
